// Logisim project mechanical_computer.circ as structural Verilog: 10 circuits, main circuit main
module main (
  input  A,
  input  B,
  input  CIN,
  input  CIN1,
  input  CIN0,
  input  A1,
  input  B1,
  input  A0,
  input  B0,
  input  CLK0,
  input  CLK1,
  input  CLK2,
  input  in_13,
  input  NA1,
  input  in_15,
  input  NB1,
  input  in_17,
  input  NA0,
  input  in_19,
  input  NB0,
  input  Drive,
  input  NDrive,
  input  OA1,
  input  in_24,
  input  OB1,
  input  in_26,
  input  OA0,
  input  in_28,
  input  OB0,
  input  in_30,
  input  ODrive,
  input  in_32,
  input  in_33,
  input  in_34,
  input  in_35,
  input  in_36,
  input  in_37,
  input  in_38,
  input  in_39,
  input  in_40,
  input  in_41,
  input  in_42,
  output O,
  output COUT,
  output O1,
  output O0,
  output COUT1,
  output COUT0,
  output out_49,
  output NO1,
  output out_51,
  output NO0,
  output OO1,
  output out_54,
  output OO0,
  output out_56,
  output out_57,
  output out_58,
  output out_59,
  output out_60
);

  wire and_1_out, and_2_out, and_block_1_o0, and_block_1_o1, and_block_3_o0, and_block_3_o1,
       decoder_dual_1_o00, decoder_dual_1_o01, decoder_dual_1_o10, decoder_dual_1_o11, decoder_dual_2_o00,
       decoder_dual_2_o01, decoder_dual_2_o10, decoder_dual_2_o11, decoder_dual_3_o00, decoder_dual_3_o01,
       decoder_dual_3_o10, decoder_dual_3_o11, decoder_dual_4_o00, decoder_dual_4_o01, decoder_dual_4_o10,
       decoder_dual_4_o11, decoder_dual_5_o00, decoder_dual_5_o01, decoder_dual_5_o10, decoder_dual_5_o11,
       decoder_dual_6_o00, decoder_dual_6_o01, decoder_dual_6_o10, decoder_dual_6_o11, decoder_dual_7_o00,
       decoder_dual_7_o01, decoder_dual_7_o10, decoder_dual_7_o11, decoder_dual_8_o00, decoder_dual_8_o01,
       decoder_dual_8_o10, decoder_dual_8_o11, decoder_dual_9_o00, decoder_dual_9_o01, decoder_dual_9_o10,
       decoder_dual_9_o11, xor_1_out, xor_block_1_o0, xor_block_1_o1;

  decoder_dual decoder_dual_1 (
    .A1(A1), .B1(B1), .A0(A0), .B0(B0), .Drive(CLK0), .O00(decoder_dual_1_o00), .O10(decoder_dual_1_o10),
    .O01(decoder_dual_1_o01), .O11(decoder_dual_1_o11));
  decoder_dual decoder_dual_2 (
    .A1(in_13), .B1(in_15), .A0(in_17), .B0(in_19), .Drive(Drive), .O00(decoder_dual_2_o00),
    .O10(decoder_dual_2_o10), .O01(decoder_dual_2_o01), .O11(decoder_dual_2_o11));
  decoder_dual decoder_dual_3 (
    .A1(OA1), .B1(OB1), .A0(OA0), .B0(OB0), .Drive(ODrive), .O00(decoder_dual_3_o00),
    .O10(decoder_dual_3_o10), .O01(decoder_dual_3_o01), .O11(decoder_dual_3_o11));
  decoder_dual decoder_dual_4 (
    .A1(in_33), .B1(in_35), .A0(in_37), .B0(in_39), .Drive(in_41), .O00(decoder_dual_4_o00),
    .O10(decoder_dual_4_o10), .O01(decoder_dual_4_o01), .O11(decoder_dual_4_o11));
  xor xor_1 (xor_1_out, A, B);
  xor_block xor_block_1 (
    .I00(decoder_dual_1_o00), .I10(decoder_dual_1_o10), .I01(decoder_dual_1_o01), .I11(decoder_dual_1_o11),
    .O1(xor_block_1_o1), .O0(xor_block_1_o0));
  and_block and_block_1 (
    .I00(decoder_dual_1_o00), .I10(decoder_dual_1_o10), .I01(decoder_dual_1_o01), .I11(decoder_dual_1_o11),
    .O1(and_block_1_o1), .O0(and_block_1_o0));
  and_block and_block_2 (
    .I00(decoder_dual_2_o00), .I10(decoder_dual_2_o10), .I01(decoder_dual_2_o01), .I11(decoder_dual_2_o11),
    .O1(out_49), .O0(out_51));
  or_block or_block_1 (
    .I00(decoder_dual_3_o00), .I10(decoder_dual_3_o10), .I01(decoder_dual_3_o01), .I11(decoder_dual_3_o11),
    .O1(OO1), .O0(OO0));
  xor_block xor_block_2 (
    .I00(decoder_dual_4_o00), .I10(decoder_dual_4_o10), .I01(decoder_dual_4_o01), .I11(decoder_dual_4_o11),
    .O1(out_57), .O0(out_59));
  xor xor_2 (O, xor_1_out, CIN);
  and and_1 (and_1_out, CIN, xor_1_out);
  and and_2 (and_2_out, B, A);
  decoder_dual decoder_dual_5 (
    .A1(xor_block_1_o1), .B1(CIN1), .A0(xor_block_1_o0), .B0(CIN0), .Drive(CLK1), .O00(decoder_dual_5_o00),
    .O10(decoder_dual_5_o10), .O01(decoder_dual_5_o01), .O11(decoder_dual_5_o11));
  or or_1 (COUT, and_1_out, and_2_out);
  xor_block xor_block_3 (
    .I00(decoder_dual_5_o00), .I10(decoder_dual_5_o10), .I01(decoder_dual_5_o01), .I11(decoder_dual_5_o11),
    .O1(O1), .O0(O0));
  and_block and_block_3 (
    .I00(decoder_dual_5_o00), .I10(decoder_dual_5_o10), .I01(decoder_dual_5_o01), .I11(decoder_dual_5_o11),
    .O1(and_block_3_o1), .O0(and_block_3_o0));
  decoder_dual decoder_dual_6 (
    .A1(and_block_3_o1), .B1(and_block_1_o1), .A0(and_block_3_o0), .B0(and_block_1_o0), .Drive(CLK2),
    .O00(decoder_dual_6_o00), .O10(decoder_dual_6_o10), .O01(decoder_dual_6_o01), .O11(decoder_dual_6_o11));
  decoder_dual decoder_dual_7 (
    .A1(NA1), .B1(NB1), .A0(NA0), .B0(NB0), .Drive(NDrive), .O00(decoder_dual_7_o00),
    .O10(decoder_dual_7_o10), .O01(decoder_dual_7_o01), .O11(decoder_dual_7_o11));
  nand_block nand_block_1 (
    .I00(decoder_dual_7_o00), .I10(decoder_dual_7_o10), .I01(decoder_dual_7_o01), .I11(decoder_dual_7_o11),
    .O1(NO1), .O0(NO0));
  decoder_dual decoder_dual_8 (
    .A1(in_24), .B1(in_26), .A0(in_28), .B0(in_30), .Drive(in_32), .O00(decoder_dual_8_o00),
    .O10(decoder_dual_8_o10), .O01(decoder_dual_8_o01), .O11(decoder_dual_8_o11));
  nor_block nor_block_1 (
    .I00(decoder_dual_8_o00), .I10(decoder_dual_8_o10), .I01(decoder_dual_8_o01), .I11(decoder_dual_8_o11),
    .O1(out_54), .O0(out_56));
  decoder_dual decoder_dual_9 (
    .A1(in_34), .B1(in_36), .A0(in_38), .B0(in_40), .Drive(in_42), .O00(decoder_dual_9_o00),
    .O10(decoder_dual_9_o10), .O01(decoder_dual_9_o01), .O11(decoder_dual_9_o11));
  xnor_block xnor_block_1 (
    .I00(decoder_dual_9_o00), .I10(decoder_dual_9_o10), .I01(decoder_dual_9_o01), .I11(decoder_dual_9_o11),
    .O1(out_58), .O0(out_60));
  or_block or_block_2 (
    .I00(decoder_dual_6_o00), .I10(decoder_dual_6_o10), .I01(decoder_dual_6_o01), .I11(decoder_dual_6_o11),
    .O1(COUT1), .O0(COUT0));

  // Notes on the sheet:
  //   AND
  //   OR
  //   XOR
  //   NOR
  //   XNOR
  //   NAND
endmodule

module lock (
  input  I1,
  input  I2,
  output O1,
  output O2
);

  wire not_1_out, not_2_out;

  Pull_Resistor pull_resistor_1 (.node(I1));
  Pull_Resistor pull_resistor_2 (.node(I2));
  and and_1 (O1, I1, not_2_out);
  not not_1 (not_1_out, O1);
  not not_2 (not_2_out, O2);
  and and_2 (O2, not_1_out, I2);
endmodule

module balence_inv (
  input  in_1,
  input  in_2,
  output out_3
);

  or or_1 (out_3, in_1, in_2);
endmodule

module decoder_dual (
  input  A1,
  input  B1,
  input  A0,
  input  B0,
  input  Drive,
  output O00,
  output O10,
  output O01,
  output O11
);

  wire lock_1_o1, lock_1_o2, lock_2_o1, lock_3_o1, lock_4_o1;

  lock lock_1 (.I1(B1), .I2(Drive), .O1(lock_1_o1), .O2(lock_1_o2));
  lock lock_2 (.I1(Drive), .I2(A0), .O1(lock_2_o1));  // open: O2
  lock lock_3 (.I1(Drive), .I2(A1), .O1(lock_3_o1));  // open: O2
  lock lock_4 (.I1(Drive), .I2(A0), .O1(lock_4_o1));  // open: O2
  lock lock_5 (.I1(A1), .I2(lock_1_o2), .O2(O00));  // open: O1
  lock lock_6 (.I1(lock_2_o1), .I2(lock_1_o1), .O1(O10));  // open: O2
  lock lock_7 (.I1(lock_3_o1), .I2(B0), .O1(O01));  // open: O2
  lock lock_8 (.I1(lock_4_o1), .I2(B0), .O1(O11));  // open: O2
endmodule

module and_block (
  input  I00,
  input  I10,
  input  I01,
  input  I11,
  output O1,
  output O0
);

  wire balence_inv_1_out_3, balence_inv_2_out_3, lock_1_o1, lock_1_o2, lock_2_o1, lock_2_o2;

  lock lock_1 (.I1(I00), .I2(I10), .O1(lock_1_o1), .O2(lock_1_o2));
  balence_inv balence_inv_1 (.in_1(lock_1_o1), .in_2(lock_1_o2), .out_3(balence_inv_1_out_3));
  lock lock_2 (.I1(balence_inv_1_out_3), .I2(I01), .O1(lock_2_o1), .O2(lock_2_o2));
  balence_inv balence_inv_2 (.in_1(lock_2_o1), .in_2(lock_2_o2), .out_3(balence_inv_2_out_3));
  lock lock_3 (.I1(I11), .I2(balence_inv_2_out_3), .O1(O1), .O2(O0));
endmodule

module nand_block (
  input  I00,
  input  I10,
  input  I01,
  input  I11,
  output O1,
  output O0
);

  wire balence_inv_1_out_3, balence_inv_2_out_3, lock_1_o1, lock_1_o2, lock_2_o1, lock_2_o2;

  lock lock_1 (.I1(I00), .I2(I10), .O1(lock_1_o1), .O2(lock_1_o2));
  lock lock_2 (.I1(balence_inv_1_out_3), .I2(I01), .O1(lock_2_o1), .O2(lock_2_o2));
  balence_inv balence_inv_1 (.in_1(lock_1_o1), .in_2(lock_1_o2), .out_3(balence_inv_1_out_3));
  balence_inv balence_inv_2 (.in_1(lock_2_o1), .in_2(lock_2_o2), .out_3(balence_inv_2_out_3));
  lock lock_3 (.I1(balence_inv_2_out_3), .I2(I11), .O1(O1), .O2(O0));
endmodule

module or_block (
  input  I00,
  input  I10,
  input  I01,
  input  I11,
  output O1,
  output O0
);

  wire balence_inv_1_out_3, balence_inv_2_out_3, lock_1_o1, lock_1_o2, lock_2_o1, lock_2_o2;

  lock lock_1 (.I1(I10), .I2(I01), .O1(lock_1_o1), .O2(lock_1_o2));
  lock lock_2 (.I1(I11), .I2(balence_inv_1_out_3), .O1(lock_2_o1), .O2(lock_2_o2));
  lock lock_3 (.I1(balence_inv_2_out_3), .I2(I00), .O1(O1), .O2(O0));
  balence_inv balence_inv_1 (.in_1(lock_1_o1), .in_2(lock_1_o2), .out_3(balence_inv_1_out_3));
  balence_inv balence_inv_2 (.in_1(lock_2_o1), .in_2(lock_2_o2), .out_3(balence_inv_2_out_3));
endmodule

module nor_block (
  input  I00,
  input  I10,
  input  I01,
  input  I11,
  output O1,
  output O0
);

  wire balence_inv_1_out_3, balence_inv_2_out_3, lock_1_o1, lock_1_o2, lock_2_o1, lock_2_o2;

  lock lock_1 (.I1(I10), .I2(I01), .O1(lock_1_o1), .O2(lock_1_o2));
  balence_inv balence_inv_1 (.in_1(lock_1_o1), .in_2(lock_1_o2), .out_3(balence_inv_1_out_3));
  lock lock_2 (.I1(I11), .I2(balence_inv_1_out_3), .O1(lock_2_o1), .O2(lock_2_o2));
  balence_inv balence_inv_2 (.in_1(lock_2_o1), .in_2(lock_2_o2), .out_3(balence_inv_2_out_3));
  lock lock_3 (.I1(I00), .I2(balence_inv_2_out_3), .O1(O1), .O2(O0));
endmodule

module xor_block (
  input  I00,
  input  I10,
  input  I01,
  input  I11,
  output O1,
  output O0
);

  wire balence_inv_1_out_3, balence_inv_2_out_3, lock_1_o1, lock_1_o2, lock_2_o1, lock_2_o2;

  lock lock_1 (.I1(I00), .I2(I11), .O1(lock_1_o1), .O2(lock_1_o2));
  balence_inv balence_inv_1 (.in_1(lock_1_o1), .in_2(lock_1_o2), .out_3(balence_inv_1_out_3));
  lock lock_2 (.I1(I10), .I2(I01), .O1(lock_2_o1), .O2(lock_2_o2));
  balence_inv balence_inv_2 (.in_1(lock_2_o1), .in_2(lock_2_o2), .out_3(balence_inv_2_out_3));
  lock lock_3 (.I1(balence_inv_2_out_3), .I2(balence_inv_1_out_3), .O1(O1), .O2(O0));
endmodule

module xnor_block (
  input  I00,
  input  I10,
  input  I01,
  input  I11,
  output O1,
  output O0
);

  wire balence_inv_1_out_3, balence_inv_2_out_3, lock_1_o1, lock_1_o2, lock_2_o1, lock_2_o2;

  lock lock_1 (.I1(I00), .I2(I11), .O1(lock_1_o1), .O2(lock_1_o2));
  balence_inv balence_inv_1 (.in_1(lock_1_o1), .in_2(lock_1_o2), .out_3(balence_inv_1_out_3));
  lock lock_2 (.I1(I10), .I2(I01), .O1(lock_2_o1), .O2(lock_2_o2));
  balence_inv balence_inv_2 (.in_1(lock_2_o1), .in_2(lock_2_o2), .out_3(balence_inv_2_out_3));
  lock lock_3 (.I1(balence_inv_1_out_3), .I2(balence_inv_2_out_3), .O1(O1), .O2(O0));
endmodule
